// Digital circuit core-vga.dig as structural Verilog
module core_vga (
  input  clk,
  input  [31:0] pc
);

  wire char, comparator_1_eq;
  wire [6:0] ScreenRam_d;

  // sync sync_1: pin names not known; wires that end beside it: clk
  ROM #(.AddrBits(12), .Bits(7)) ScreenRam (.sel(1'b1), .D(ScreenRam_d));  // open: A
  Comparator #(.Bits(12)) comparator_1 (.a({12{1'b0}}), .eq(comparator_1_eq));  // open: b, gt, lt
  Multiplexer multiplexer_1 (.sel(comparator_1_eq), .in_0(ScreenRam_d[0]), .in_1(pc[0]), .out(char));
  // textMode textmode_1: pin names not known; wires that end beside it: char, clk
  VGA vga_1 ();  // open: R, G, B, H, V, C
  // Pins of 1 and 7 bits meet at ScreenRam_d
  // Pins of 1 and 32 bits meet at pc
endmodule
