// Digital circuit control unit.dig as structural Verilog
module control_unit (
  input  [6:0] opcode,
  input  [2:0] funct3,
  input  [6:0] funct7,
  output [3:0] alu_op,
  output need_imm,
  output [2:0] immOp,
  output [3:0] BranchOp,
  output need_write,
  output salta,
  output [1:0] memoOp,
  output need_memo
);

  wire add, add_sub, addi, \and , andi, auipc, beq, bge, bgeu, blt, bltu, bne, ecall_ibreak, funct3_2_eq,
       funct3_3_eq, funct3_4_eq, funct3_5_eq, funct3_6_eq, funct3_7_eq, funct3_8_eq, funct3_9_eq,
       funct3_10_eq, funct3_11_eq, funct3_12_eq, funct3_13_eq, funct3_14_eq, funct3_15_eq, funct3_16_eq,
       funct3_17_eq, funct3_18_eq, funct3_19_eq, funct3_20_eq, funct3_21_eq, funct3_22_eq, funct3_23_eq,
       funct3_24_eq, funct3_25_eq, funct3_26_eq, funct3_27_eq, funct3_28_eq, funct3_29_eq, funct3_30_eq,
       funct3_31_eq, funct3_32_eq, funct3_eq, funct7_eq, i, i_arith, i_jalr, i_load, i_pc, is_contrary,
       is_i_arith, is_r_arith, jal, jalr, lb, lbu, lh, lhu, lui, lw, not_1_out, not_2_out, not_3_out, \or ,
       ori, r, s, sb, sh, sll, slli, slr, slt, slti, sltiu, sltu, sra, srai, srl_sra, srli, srli_srai, sub,
       sub_sra, sw, u, \xor , xori;
  wire [1:0] load, store;
  wire [2:0] add_1_s, add_3_s, add_4_s, immOp1, immOp2, immOp3, immOp4, immOp5;
  wire [3:0] demultiplexer_1_out_1, demultiplexer_2_out_1;

  or or_1 (is_contrary, sub, sra, srai);
  or or_2 (is_r_arith, add, sub, \xor , \or , \and , sll, slr, sra, slt, sltu);
  or or_3 (is_i_arith, addi, xori, ori, andi, slli, srli, srai, slti, sltiu);
  or or_4 (i, i_arith, i_load, i_jalr, i_pc);
  or or_5 (u, lui, auipc);
  or or_6 (need_imm, i, s, salta, u, jal);
  or or_7 (need_write, r, i, u, jal);
  or or_8 (need_memo, i_load, s);
  Comparator #(.Bits(7)) type_r (.a(opcode), .b(7'b0110011), .eq(r));  // open: gt, lt
  Comparator #(.Bits(7)) type_i_arith (.a(opcode), .b(7'b0010011), .eq(i_arith));  // open: gt, lt
  Comparator #(.Bits(7)) type_i_load (.a(opcode), .b(7'b0000011), .eq(i_load));  // open: gt, lt
  Comparator #(.Bits(7)) type_i_jalr (.a(opcode), .b(7'b1100111), .eq(i_jalr));  // open: gt, lt
  Comparator #(.Bits(7)) type_i_pc (.a(opcode), .b(7'b1110011), .eq(i_pc));  // open: gt, lt
  Comparator #(.Bits(7)) type_s (.a(opcode), .b(7'b0100011), .eq(s));  // open: gt, lt
  Comparator #(.Bits(7)) type_b (.a(opcode), .b(7'b1100011), .eq(salta));  // open: gt, lt
  Comparator #(.Bits(7)) type_u_lui (.a(opcode), .b(7'b0110111), .eq(lui));  // open: gt, lt
  Comparator #(.Bits(7)) type_u_auipc (.a(opcode), .b(7'b0010111), .eq(auipc));  // open: gt, lt
  Comparator #(.Bits(7)) type_j (.a(opcode), .b(7'b1101111), .eq(jal));  // open: gt, lt
  Demultiplexer #(.Bits(3)) demultiplexer_1 (
    .sel(is_r_arith), .in(funct3), .out_1(demultiplexer_1_out_1[2:0]));  // open: out_0
  Demultiplexer #(.Bits(3)) demultiplexer_2 (
    .sel(is_i_arith), .in(funct3), .out_1(demultiplexer_2_out_1[2:0]));  // open: out_0
  Add #(.Bits(3)) add_1 (.a(immOp1), .b(immOp2), .c_i(1'b0), .s(add_1_s));  // open: c_o
  Demultiplexer #(.Bits(3)) demultiplexer_3 (.sel(i), .in(3'b001), .out_1(immOp1));  // open: out_0
  Add #(.Bits(2)) add_2 (.a(store), .b(load), .c_i(1'b0), .s(memoOp));  // open: c_o
  Demultiplexer #(.Bits(2)) demultiplexer_4 (.sel(i_load), .in(2'b01), .out_1(load));  // open: out_0
  Multiplexer multiplexer_1 (.sel(is_contrary), .in_0(1'b0), .in_1(1'b1), .out(demultiplexer_1_out_1[3]));
  Multiplexer multiplexer_2 (.sel(is_contrary), .in_0(1'b0), .in_1(1'b1), .out(demultiplexer_2_out_1[3]));
  Multiplexer #(.Bits(4)) multiplexer_3 (
    .sel(is_i_arith), .in_0(demultiplexer_1_out_1), .in_1(demultiplexer_2_out_1), .out(alu_op));
  Add #(.Bits(3)) add_3 (.a(immOp3), .b(add_1_s), .c_i(1'b0), .s(add_3_s));  // open: c_o
  Demultiplexer #(.Bits(3)) demultiplexer_5 (.sel(s), .in(3'b010), .out_1(immOp2));  // open: out_0
  Demultiplexer #(.Bits(2)) demultiplexer_6 (.sel(s), .in(2'b10), .out_1(store));  // open: out_0
  Add #(.Bits(3)) add_4 (.a(immOp4), .b(add_3_s), .c_i(1'b0), .s(add_4_s));  // open: c_o
  Demultiplexer #(.Bits(3)) demultiplexer_7 (.sel(salta), .in(3'b011), .out_1(immOp3));  // open: out_0
  Comparator #(.Bits(3)) u_funct3 (.a(funct3), .b(3'b000), .eq(funct3_eq));  // open: gt, lt
  Comparator #(.Bits(7)) u_funct7 (.a(funct7), .b(7'b0100000), .eq(funct7_eq));  // open: gt, lt
  Comparator #(.Bits(3)) funct3_2 (.a(funct3), .b(3'b000), .eq(funct3_2_eq));  // open: gt, lt
  and and_1 (srai, funct7[5], i_arith, srli_srai);
  not not_1 (not_1_out, funct7[5]);
  Comparator #(.Bits(3)) funct3_3 (.a(funct3), .b(3'b000), .eq(funct3_3_eq));  // open: gt, lt
  Comparator #(.Bits(3)) funct3_4 (.a(funct3), .b(3'b000), .eq(funct3_4_eq));  // open: gt, lt
  Comparator #(.Bits(3)) funct3_5 (.a(funct3), .b(3'b000), .eq(funct3_5_eq));  // open: gt, lt
  Comparator #(.Bits(3)) funct3_6 (.a(funct3), .b(3'b000), .eq(funct3_6_eq));  // open: gt, lt
  Comparator #(.Bits(3)) funct3_7 (.a(funct3), .b(3'b000), .eq(funct3_7_eq));  // open: gt, lt
  and and_2 (add_sub, funct3_eq, r);
  and and_3 (sub_sra, funct7_eq, r);
  and and_4 (addi, funct3_2_eq, i_arith);
  and and_5 (srli, srli_srai, not_1_out, i_arith);
  and and_6 (lb, funct3_3_eq, i_load);
  and and_7 (jalr, funct3_4_eq, i_jalr);
  and and_8 (ecall_ibreak, funct3_5_eq, i_pc);
  and and_9 (sb, funct3_6_eq, s);
  and and_10 (beq, funct3_7_eq, salta);
  Multiplexer #(.Bits(3)) multiplexer_4 (.sel(salta), .in_0(3'b010), .in_1(funct3), .out(BranchOp[2:0]));
  Add #(.Bits(3)) add_5 (.a(immOp5), .b(add_4_s), .c_i(1'b0), .s(immOp));  // open: c_o
  Demultiplexer #(.Bits(3)) demultiplexer_8 (.sel(u), .in(3'b100), .out_1(immOp4));  // open: out_0
  or or_9 (BranchOp[3], jal, i_jalr);
  Comparator #(.Bits(3)) funct3_8 (.a(funct3), .b(3'b100), .eq(funct3_8_eq));  // open: gt, lt
  Comparator #(.Bits(3)) funct3_9 (.a(funct3), .b(3'b100), .eq(funct3_9_eq));  // open: gt, lt
  Demultiplexer #(.Bits(3)) demultiplexer_9 (.sel(jal), .in(3'b111), .out_1(immOp5));  // open: out_0
  and and_11 (sub, sub_sra, r, add_sub);
  and and_12 (add, add_sub, r, not_2_out);
  not not_2 (not_2_out, sub);
  Comparator #(.Bits(3)) funct3_10 (.a(funct3), .b(3'b001), .eq(funct3_10_eq));  // open: gt, lt
  Comparator #(.Bits(3)) funct3_11 (.a(funct3), .b(3'b001), .eq(funct3_11_eq));  // open: gt, lt
  Comparator #(.Bits(3)) funct3_12 (.a(funct3), .b(3'b001), .eq(funct3_12_eq));  // open: gt, lt
  and and_13 (\xor , funct3_8_eq, r);
  and and_14 (xori, funct3_9_eq, i_arith);
  and and_15 (lh, funct3_10_eq, i_load);
  and and_16 (sh, funct3_11_eq, s);
  and and_17 (bne, funct3_12_eq, salta);
  Comparator #(.Bits(3)) funct3_13 (.a(funct3), .b(3'b110), .eq(funct3_13_eq));  // open: gt, lt
  and and_18 (sra, sub_sra, r, srl_sra);
  and and_19 (slr, srl_sra, r, not_3_out);
  not not_3 (not_3_out, sra);
  Comparator #(.Bits(3)) funct3_14 (.a(funct3), .b(3'b110), .eq(funct3_14_eq));  // open: gt, lt
  Comparator #(.Bits(3)) funct3_15 (.a(funct3), .b(3'b010), .eq(funct3_15_eq));  // open: gt, lt
  Comparator #(.Bits(3)) funct3_16 (.a(funct3), .b(3'b010), .eq(funct3_16_eq));  // open: gt, lt
  Comparator #(.Bits(3)) funct3_17 (.a(funct3), .b(3'b100), .eq(funct3_17_eq));  // open: gt, lt
  and and_20 (\or , funct3_13_eq, r);
  and and_21 (ori, funct3_14_eq, i_arith);
  and and_22 (lw, funct3_15_eq, i_load);
  and and_23 (sw, funct3_16_eq, s);
  and and_24 (blt, funct3_17_eq, salta);
  Comparator #(.Bits(3)) funct3_18 (.a(funct3), .b(3'b111), .eq(funct3_18_eq));  // open: gt, lt
  Comparator #(.Bits(3)) funct3_19 (.a(funct3), .b(3'b111), .eq(funct3_19_eq));  // open: gt, lt
  Comparator #(.Bits(3)) funct3_20 (.a(funct3), .b(3'b100), .eq(funct3_20_eq));  // open: gt, lt
  Comparator #(.Bits(3)) funct3_21 (.a(funct3), .b(3'b101), .eq(funct3_21_eq));  // open: gt, lt
  and and_25 (\and , funct3_18_eq, r);
  and and_26 (andi, funct3_19_eq, i_arith);
  and and_27 (lbu, funct3_20_eq, i_load);
  and and_28 (bge, funct3_21_eq, salta);
  Comparator #(.Bits(3)) funct3_22 (.a(funct3), .b(3'b001), .eq(funct3_22_eq));  // open: gt, lt
  Comparator #(.Bits(3)) funct3_23 (.a(funct3), .b(3'b001), .eq(funct3_23_eq));  // open: gt, lt
  and and_29 (sll, funct3_22_eq, r);
  Comparator #(.Bits(3)) funct3_24 (.a(funct3), .b(3'b110), .eq(funct3_24_eq));  // open: gt, lt
  and and_30 (slli, funct3_23_eq, i_arith);
  Comparator #(.Bits(3)) funct3_25 (.a(funct3), .b(3'b101), .eq(funct3_25_eq));  // open: gt, lt
  and and_31 (bltu, funct3_24_eq, salta);
  and and_32 (lhu, funct3_25_eq, i_load);
  Comparator #(.Bits(3)) funct3_26 (.a(funct3), .b(3'b101), .eq(funct3_26_eq));  // open: gt, lt
  Comparator #(.Bits(3)) funct3_27 (.a(funct3), .b(3'b101), .eq(funct3_27_eq));  // open: gt, lt
  and and_33 (srl_sra, funct3_26_eq, r);
  and and_34 (srli_srai, funct3_27_eq, i_arith);
  Comparator #(.Bits(3)) funct3_28 (.a(funct3), .b(3'b111), .eq(funct3_28_eq));  // open: gt, lt
  and and_35 (bgeu, funct3_28_eq, salta);
  Comparator #(.Bits(3)) funct3_29 (.a(funct3), .b(3'b010), .eq(funct3_29_eq));  // open: gt, lt
  Comparator #(.Bits(3)) funct3_30 (.a(funct3), .b(3'b010), .eq(funct3_30_eq));  // open: gt, lt
  and and_36 (slt, funct3_29_eq, r);
  and and_37 (slti, funct3_30_eq, i_arith);
  Comparator #(.Bits(3)) funct3_31 (.a(funct3), .b(3'b011), .eq(funct3_31_eq));  // open: gt, lt
  Comparator #(.Bits(3)) funct3_32 (.a(funct3), .b(3'b011), .eq(funct3_32_eq));  // open: gt, lt
  and and_38 (sltu, funct3_31_eq, r);
  and and_39 (sltiu, funct3_32_eq, i_arith);

  // Other names for the same wires on the sheet: b = salta; imm_i_arith = funct7[5]
endmodule
