// Digital circuit core.dig as structural Verilog
module core (
  input  clk,
  output [31:0] out
);

  wire branch_1_out, load_from_memo, lui, multiplexer_3_out, need_imm, need_memo, need_write, pc_plus_4,
       salta;
  wire [2:0] funct3, immOp;
  wire [3:0] alu_op, BranchOp, memoOp;
  wire [4:0] rd, rs1, rs2;
  wire [6:0] funct7, opcode;
  wire [31:0] A, B, dataRdMemo, imm, multiplexer_1_out, multiplexer_2_out, multiplexer_6_out,
       multiplexer_7_out, pc_1_out, r1Data, r2Data, sum_s;

  PC pc_1 (.in(multiplexer_7_out), .clk(clk), .out(pc_1_out));
  Add #(.Bits(32)) sum (.a(pc_1_out), .b(32'h4), .c_i(1'b0), .s(sum_s));  // open: c_o
  Insts_Memory insts_memory_1 (.pc(pc_1_out), .out({funct7, rs2, rs1, funct3, rd, opcode}));
  Multiplexer #(.Bits(32)) multiplexer_1 (.sel(pc_plus_4), .in_0(out), .in_1(sum_s), .out(multiplexer_1_out));
  ImmGenerator immgenerator_1 (.inst({funct7, rs2, rs1, funct3, rd}), .ImmOp(immOp), .imm(imm));
  // control_unit control_unit_1: pin names not known; wires that end beside it: opcode, funct3, funct7, alu_op, need_imm, immOp, BranchOp, need_write, salta, need_memo, memoOp, load_from_memo, pc_plus_4, lui
  Multiplexer #(.Bits(32)) multiplexer_2 (
    .sel(load_from_memo), .in_0(multiplexer_1_out), .in_1(dataRdMemo), .out(multiplexer_2_out));
  Multiplexer multiplexer_3 (.sel(lui), .in_0(multiplexer_2_out[0]), .in_1(imm[0]), .out(multiplexer_3_out));
  // register_unit register_unit_1: pin names not known; wires that end beside it: multiplexer_3_out, rs1, rs2, rd, clk, need_write, r1Data, r2Data
  data_memory data_memory_1 (.adress(out), .rs(r1Data), .memoOp(memoOp), .clk(clk), .dataRd(dataRdMemo));
  Multiplexer #(.Bits(32)) multiplexer_4 (.sel(salta), .in_0(r1Data), .in_1(pc_1_out), .out(A));
  Multiplexer #(.Bits(32)) multiplexer_5 (.sel(need_imm), .in_0(r2Data), .in_1(imm), .out(B));
  Multiplexer #(.Bits(32)) multiplexer_6 (.sel(need_memo), .in_0(A), .in_1(r2Data), .out(multiplexer_6_out));
  Branch branch_1 (.rs1(r1Data), .rs2(r2Data), .BrOp(BranchOp), .out(branch_1_out));
  ALU alu_1 (.A(multiplexer_6_out), .B(B), .alu_op(alu_op), .out(out));
  Multiplexer #(.Bits(32)) multiplexer_7 (.sel(branch_1_out), .in_0(sum_s), .in_1(out), .out(multiplexer_7_out));
  // Pins of 1 and 32 bits meet at imm
  // Pins of 1 and 32 bits meet at multiplexer_2_out

  // Other names for the same wires on the sheet: AluOut[31:0] = out
endmodule
